# Fritzing sketch Morse Code _ Sender + receiver (saved by Fritzing 0.9.3b)
perfboards: 2

parts:
  Part2 = Arduino Nano (Rev3.0)
  LED2 = smd LED [color="Red (633nm)" package="1206 [SMD]"]
  Part3 = Arduino Nano (Rev3.0)
  R3 = Resistor [tolerance=±5% resistance=220 package="0402 [SMD]"]
  LCD2 = LCD screen
  LCM1602_IIC2 = LCM1602 IIC [part_number="LCM1602 IIC" chip_label="LCM1602 IIC" package="DIP (Dual Inline) [THT]"]
  R4 = Rotary Potentiometer (Small) [maximum_resistance=100kΩ package=THT]
  R5 = PHOTOCELL [package=photocell]
  J1 = male pin header, 1 pin [form="♂ (male)"]
  J2 = male pin header, 1 pin [form="♂ (male)"]
  J3 = male pin header, 1 pin [form="♂ (male)"]
  J4 = male pin header, 1 pin [form="♂ (male)"]
  R2 = Resistor [tolerance=±5% resistance=220 package="0402 [SMD]"]

nets (from the breadboard view):
  N1: Part2.GND, LED2.anode
  N2: Part2.D12/MISO, R2.Pin_1
  N3: LED2.cathode, R2.Pin_0
  N4: Part3.A1, R4.wiper
  N5: Part3.A0, R3.Pin_1, LCM1602_IIC2.GND, R4.leg1, J4.pin1
  N6: R3.Pin_0, R5.P$2
  VSS: LCD2.VSS, LCM1602_IIC2.VSS
  VDD: LCD2.VDD, LCM1602_IIC2.VDD
  N7: LCD2.V0, LCM1602_IIC2.V0
  N8: LCD2.RS, LCM1602_IIC2.RS
  N9: LCD2.R/W, LCM1602_IIC2.RW
  N10: LCD2.E, LCM1602_IIC2.E
  N11: LCD2.DB0, LCM1602_IIC2.D0
  N12: LCD2.DB1, LCM1602_IIC2.D1
  N13: LCD2.DB2, LCM1602_IIC2.D2
  N14: LCD2.DB3, LCM1602_IIC2.D3
  N15: LCD2.DB4, LCM1602_IIC2.D4
  N16: LCD2.DB5, LCM1602_IIC2.D5
  N17: LCD2.DB6, LCM1602_IIC2.D6
  N18: LCD2.DB7, LCM1602_IIC2.D7
  N19: LCD2.LED+, LCM1602_IIC2.A
  N20: LCD2.LED-, LCM1602_IIC2.K
  N21: LCM1602_IIC2.VCC, R4.leg2, R5.P$1, J3.pin1
  N22: LCM1602_IIC2.SDA, J2.pin1
  N23: LCM1602_IIC2.SCL, J1.pin1
  N24: LCM1602_IIC2.LED_A, LCM1602_IIC2.LED_B

custom parts:
  LCM1602 IIC: I2C-Module to use a 1602 or 2004 LCD on with the wire.h libory Serial LCD Modul
