# Fritzing sketch Circuit_transceiver (saved by Fritzing 0.9.4)
breadboards: 2

parts:
  Part1 = Arduino Uno (Rev3)
  R1 = PHOTOCELL [package=photocell-kit]
  LED1 = LEDs [package=led10mm]
  R2 = Resistor [tolerance=±5% resistance=220 package="2010 [SMD]"]
  R3 = Resistor [tolerance=±5% resistance=220 package="2010 [SMD]"]
  LCD2 = LCD screen
  LCM1602_IIC2 = LCM1602 IIC [part_number="LCM1602 IIC" chip_label="LCM1602 IIC" package="DIP (Dual Inline) [THT]"]

nets:
  N1: Part1.A1, R1.P$1, R3.Pin_1
  N2: Part1.A4/SDA, LCM1602_IIC2.SDA
  N3: Part1.A5/SCL, LCM1602_IIC2.SCL
  N4: Part1.D12/MISO, R2.Pin_0
  GND: Part1.GND, LED1.C, R3.Pin_0, LCM1602_IIC2.GND
  5V: Part1.5V, R1.P$2, LCM1602_IIC2.VCC
  N5: LED1.A, R2.Pin_1
  VSS: LCD2.VSS, LCM1602_IIC2.VSS
  VDD: LCD2.VDD, LCM1602_IIC2.VDD
  N6: LCD2.V0, LCM1602_IIC2.V0
  N7: LCD2.RS, LCM1602_IIC2.RS
  N8: LCD2.R/W, LCM1602_IIC2.RW
  N9: LCD2.E, LCM1602_IIC2.E
  N10: LCD2.DB0, LCM1602_IIC2.D0
  N11: LCD2.DB1, LCM1602_IIC2.D1
  N12: LCD2.DB2, LCM1602_IIC2.D2
  N13: LCD2.DB3, LCM1602_IIC2.D3
  N14: LCD2.DB4, LCM1602_IIC2.D4
  N15: LCD2.DB5, LCM1602_IIC2.D5
  N16: LCD2.DB6, LCM1602_IIC2.D6
  N17: LCD2.DB7, LCM1602_IIC2.D7
  N18: LCD2.LED+, LCM1602_IIC2.A
  N19: LCD2.LED-, LCM1602_IIC2.K
  N20: LCM1602_IIC2.LED_A, LCM1602_IIC2.LED_B

custom parts:
  LCM1602 IIC: I2C-Module to use a 1602 or 2004 LCD on with the wire.h libory Serial LCD Modul
